// Logisim project ALU(1).circ as structural Verilog: 2 circuits, main circuit main
module ALU8 (
  input  [7:0] A,
  input  [7:0] B,
  input  [3:0] OP,
  output [7:0] RESULT,
  output Z,
  output N,
  output V,
  output C,
  output GT,
  output EQ,
  output LT
);

  wire and_2_out, not_3_out, undriven_2;
  wire [7:0] undriven;

  // NOT_Gate not_1 has open pins: in=open, out=A[7]
  and and_1 (A[7], A[7], A[7], not_3_out);
  // NOT_Gate not_2 has open pins: in=open, out=A[7]
  and and_2 (and_2_out, A[7], A[7], undriven_2);
  or or_1 (V, A[7], and_2_out);
  Multiplexer #(.select(4), .width(8)) multiplexer_1 (.out({N, RESULT[6:0]}));  // open: in0, in1, in2, in3, in4, in5, in6, in7, in8, in9, in10, in11, in12, in13, in14, in15, sel
  Adder adder_1 (.a(A), .b({A[7], B[6:0]}));  // open: out, cin, cout
  Adder adder_2 (.a(undriven));  // open: b, out, cin, cout
  Subtractor subtractor_1 (.a(undriven));  // open: b, out, bin, bout
  Comparator comparator_1 (.a({N, RESULT[6:0]}), .b({8{1'b0}}), .eq(Z));  // open: gt, lt
  Comparator comparator_2 (.gt(GT), .eq(EQ), .lt(LT));  // open: a, b
  // NOT_Gate not_3 has open pins: in=open, out=not_3_out

  assign B[7] = A[7];
  assign RESULT[7] = N;

  // Other names for the same wires on the sheet: B7 = A[7]
endmodule

module main (
  input  [7:0] A_7_0,
  input  [7:0] B_7_0,
  input  [3:0] OP_3_0,
  input  S0,
  input  S1,
  input  S2,
  input  S3,
  input  LOAD_OUT,
  input  [7:0] IN_A,
  input  LOAD_A,
  input  [7:0] IN_B,
  input  LOAD_B,
  output [7:0] OUT_7_0,
  output [7:0] OUT_BUS,
  output LT,
  output EQ,
  output GT
);

  wire [7:0] A_BUS, ADD, ALU_OUT, AND_BLOCK_out, B_BUS, DEC, INC, NOT_BLOCK_out, NOT_FOR_DEC_out,
       OR_BLOCK_out, shifter_1_out, shifter_2_out;

  assign NOT_FOR_DEC_out = ~8'h1;  // NOT_Gate NOT_FOR_DEC, 8 bits wide
  Adder adder_1 (.a(A_BUS), .b(B_BUS), .out(ADD));  // open: cin, cout
  Adder adder_2 (.a(A_BUS), .b(8'h1), .out(INC));  // open: cin, cout
  Adder adder_3 (.a(A_BUS), .b(NOT_FOR_DEC_out), .out(DEC), .cin(1'b0));  // open: cout
  assign NOT_BLOCK_out = ~A_BUS;  // NOT_Gate NOT_BLOCK, 8 bits wide
  assign AND_BLOCK_out = A_BUS & B_BUS;  // AND_Gate AND_BLOCK, 8 bits wide
  assign OR_BLOCK_out = A_BUS | B_BUS;  // OR_Gate OR_BLOCK, 8 bits wide
  Shifter shifter_1 (.in(A_BUS), .\dist (3'b001), .out(shifter_1_out));
  Shifter #(.shift("lr")) shifter_2 (.in(A_BUS), .\dist (3'b001), .out(shifter_2_out));
  Comparator comparator_1 (.a(A_BUS), .b(B_BUS), .gt(GT), .eq(EQ), .lt(LT));
  Multiplexer #(.select(4), .width(8)) multiplexer_1 (
    .in0(ADD), .in1(INC), .in2(DEC), .in3(NOT_BLOCK_out), .in4(AND_BLOCK_out), .in5(OR_BLOCK_out),
    .in6(shifter_1_out), .in7(shifter_2_out), .in8({{5{1'b0}}, GT, LT, EQ}), .in9(B_BUS), .in10({8{1'b0}}),
    .in11({8{1'b0}}), .in12({8{1'b0}}), .in13(A_BUS), .in14({8{1'b0}}), .in15({8{1'b0}}), .out(OUT_7_0),
    .sel(OP_3_0));
  LED led_1 (.in(ALU_OUT[5]));
  LED led_2 (.in(ALU_OUT[4]));
  LED led_3 (.in(ALU_OUT[3]));
  LED led_4 (.in(ALU_OUT[1]));
  LED led_5 (.in(ALU_OUT[0]));
  LED led_6 (.in(ALU_OUT[7]));
  LED led_7 (.in(ALU_OUT[6]));
  LED led_8 (.in(ALU_OUT[2]));
  Register #(.width(8)) REG_OUT (.D(OUT_7_0), .en(LOAD_OUT), .clk(1'b0), .Q(OUT_BUS), .clr(1'b0));
  Register #(.width(8)) REG_A (.D(IN_A), .en(LOAD_A), .clk(1'b0), .Q(A_BUS), .clr(1'b0));
  Register #(.width(8)) REG_B (.D(IN_B), .en(LOAD_B), .clk(1'b0), .Q(B_BUS), .clr(1'b0));

  assign S0 = OP_3_0[3];
  assign S1 = OP_3_0[2];
  assign S2 = OP_3_0[1];
  assign S3 = OP_3_0[0];

  // Other names for the same wires on the sheet: EQ_FLAG = EQ; LT_FLAG = LT; GT_FLAG = GT; OUT_BUS_t[7:0] = OUT_7_0

  // Notes on the sheet:
  //   CONST_0
  //   CONST_1
  //   Adder8
  //   INC_ADDER
  //   DEC_ADDER
  //   SHL_BLOCK
  //   SHR_BLOCK
  //   CMP_BLOCK
  //   CONST_255 
  //   ZERO8
  //   CMP_OUT
  //   Bit7
  //   Bit6
  //   Bit5
  //   Bit4
  //   Bit3
endmodule
